// Logisim project memoria.circ as structural Verilog: 2 circuits, main circuit main
module main (
  input  in_1,
  input  in_2,
  input  in_3,
  input  in_4,
  input  in_5,
  input  in_6,
  input  in_7,
  input  in_8
);

  wire and_1_out, and_2_out, and_3_out, and_4_out, and_5_out, and_6_out, and_7_out, and_8_out, and_9_out,
       and_10_out, and_11_out, and_12_out, and_13_out, and_14_out, and_15_out, and_16_out, d_ff_23_p3,
       not_2_out, not_3_out, not_4_out, not_5_out, not_6_out, not_7_out, not_8_out, not_9_out, not_10_out,
       not_11_out, not_12_out, not_13_out, not_14_out, not_15_out, not_16_out;

  // NOT_Gate not_1 is placed but not wired
  not not_2 (not_2_out, in_5);
  not not_3 (not_3_out, in_6);
  not not_4 (not_4_out, in_7);
  not not_5 (not_5_out, in_8);
  not not_6 (not_6_out, in_5);
  not not_7 (not_7_out, in_6);
  not not_8 (not_8_out, in_7);
  not not_9 (not_9_out, in_5);
  not not_10 (not_10_out, in_6);
  not not_11 (not_11_out, in_8);
  not not_12 (not_12_out, in_5);
  not not_13 (not_13_out, in_6);
  not not_14 (not_14_out, in_5);
  not not_15 (not_15_out, in_7);
  not not_16 (not_16_out, in_8);
  and and_1 (and_1_out, not_2_out, not_3_out, not_4_out, not_5_out);
  and and_2 (and_2_out, not_6_out, not_7_out, not_8_out, in_8);
  and and_3 (and_3_out, not_9_out, not_10_out, in_7, not_11_out);
  and and_4 (and_4_out, not_12_out, not_13_out, in_7, in_8);
  and and_5 (and_5_out, not_14_out, in_6, not_15_out, not_16_out);
  // AND_Gate and_6 has open pins: out=and_6_out
  // AND_Gate and_7 has open pins: out=and_7_out
  // AND_Gate and_8 has open pins: out=and_8_out
  // AND_Gate and_9 has open pins: out=and_9_out
  // AND_Gate and_10 has open pins: out=and_10_out
  // AND_Gate and_11 has open pins: out=and_11_out
  // AND_Gate and_12 has open pins: out=and_12_out
  // AND_Gate and_13 has open pins: out=and_13_out
  // AND_Gate and_14 has open pins: out=and_14_out
  // AND_Gate and_15 has open pins: out=and_15_out
  // AND_Gate and_16 has open pins: out=and_16_out
  D_Flip_Flop d_ff_1 (.clk(and_1_out), .D(in_4));  // open: Q, Qn, preset, en, reset
  D_Flip_Flop d_ff_2 (.clk(and_2_out), .D(in_4));  // open: Q, Qn, preset, en, reset
  D_Flip_Flop d_ff_3 (.clk(and_3_out), .D(in_4));  // open: Q, Qn, preset, en, reset
  D_Flip_Flop d_ff_4 (.clk(and_4_out), .D(in_4));  // open: Q, Qn, preset, en, reset
  D_Flip_Flop d_ff_5 (.clk(and_5_out), .D(in_4));  // open: Q, Qn, preset, en, reset
  D_Flip_Flop d_ff_6 (.clk(and_6_out), .D(in_4));  // open: Q, Qn, preset, en, reset
  D_Flip_Flop d_ff_7 (.clk(and_7_out), .D(in_4));  // open: Q, Qn, preset, en, reset
  D_Flip_Flop d_ff_8 (.clk(and_8_out), .D(in_4));  // open: Q, Qn, preset, en, reset
  D_Flip_Flop d_ff_9 (.clk(and_9_out), .D(in_4));  // open: Q, Qn, preset, en, reset
  D_Flip_Flop d_ff_10 (.clk(and_10_out), .D(in_4));  // open: Q, Qn, preset, en, reset
  D_Flip_Flop d_ff_11 (.clk(and_11_out), .D(in_4));  // open: Q, Qn, preset, en, reset
  D_Flip_Flop d_ff_12 (.clk(and_12_out), .D(in_4));  // open: Q, Qn, preset, en, reset
  D_Flip_Flop d_ff_13 (.clk(and_13_out), .D(in_4));  // open: Q, Qn, preset, en, reset
  D_Flip_Flop d_ff_14 (.clk(and_14_out), .D(in_4));  // open: Q, Qn, preset, en, reset
  D_Flip_Flop d_ff_15 (.clk(and_15_out), .D(in_4));  // open: Q, Qn, preset, en, reset
  D_Flip_Flop d_ff_16 (.clk(and_16_out), .D(in_4));  // open: Q, Qn, preset, en, reset
  D_Flip_Flop d_ff_17 (.clk(and_1_out), .D(in_3));  // open: Q, Qn, preset, en, reset
  D_Flip_Flop d_ff_18 (.clk(and_2_out), .D(in_3));  // open: Q, Qn, preset, en, reset
  D_Flip_Flop d_ff_19 (.clk(and_3_out), .D(in_3));  // open: Q, Qn, preset, en, reset
  D_Flip_Flop d_ff_20 (.clk(and_4_out), .D(in_3));  // open: Q, Qn, preset, en, reset
  D_Flip_Flop d_ff_21 (.clk(and_5_out), .D(in_3));  // open: Q, Qn, preset, en, reset
  D_Flip_Flop d_ff_22 (.clk(and_6_out), .D(in_3));  // open: Q, Qn, preset, en, reset
  // D_Flip_Flop d_ff_23: pin names not known; wires that end beside it: and_7_out, in_3, d_ff_23_p3, d_ff_23_p3
  D_Flip_Flop d_ff_24 (.clk(and_8_out), .D(in_3));  // open: Q, Qn, preset, en, reset
  D_Flip_Flop d_ff_25 (.clk(and_9_out), .D(in_3));  // open: Q, Qn, preset, en, reset
  D_Flip_Flop d_ff_26 (.clk(and_10_out), .D(in_3));  // open: Q, Qn, preset, en, reset
  D_Flip_Flop d_ff_27 (.clk(and_11_out), .D(in_3));  // open: Q, Qn, preset, en, reset
  D_Flip_Flop d_ff_28 (.clk(and_12_out), .D(in_3));  // open: Q, Qn, preset, en, reset
  D_Flip_Flop d_ff_29 (.clk(and_13_out), .D(in_3));  // open: Q, Qn, preset, en, reset
  D_Flip_Flop d_ff_30 (.clk(and_14_out), .D(in_3));  // open: Q, Qn, preset, en, reset
  D_Flip_Flop d_ff_31 (.clk(and_15_out), .D(in_3));  // open: Q, Qn, preset, en, reset
  D_Flip_Flop d_ff_32 (.clk(and_16_out), .D(in_3));  // open: Q, Qn, preset, en, reset
  D_Flip_Flop d_ff_33 (.clk(and_1_out), .D(in_2));  // open: Q, Qn, preset, en, reset
  D_Flip_Flop d_ff_34 (.clk(and_2_out), .D(in_2));  // open: Q, Qn, preset, en, reset
  D_Flip_Flop d_ff_35 (.clk(and_3_out), .D(in_2));  // open: Q, Qn, preset, en, reset
  D_Flip_Flop d_ff_36 (.clk(and_4_out), .D(in_2));  // open: Q, Qn, preset, en, reset
  D_Flip_Flop d_ff_37 (.clk(and_5_out), .D(in_2));  // open: Q, Qn, preset, en, reset
  D_Flip_Flop d_ff_38 (.clk(and_6_out), .D(in_2));  // open: Q, Qn, preset, en, reset
  D_Flip_Flop d_ff_39 (.clk(and_7_out), .D(in_2));  // open: Q, Qn, preset, en, reset
  D_Flip_Flop d_ff_40 (.clk(and_8_out), .D(in_2));  // open: Q, Qn, preset, en, reset
  D_Flip_Flop d_ff_41 (.clk(and_9_out), .D(in_2));  // open: Q, Qn, preset, en, reset
  D_Flip_Flop d_ff_42 (.clk(and_10_out), .D(in_2));  // open: Q, Qn, preset, en, reset
  D_Flip_Flop d_ff_43 (.clk(and_11_out), .D(in_2));  // open: Q, Qn, preset, en, reset
  D_Flip_Flop d_ff_44 (.clk(and_12_out), .D(in_2));  // open: Q, Qn, preset, en, reset
  D_Flip_Flop d_ff_45 (.clk(and_13_out), .D(in_2));  // open: Q, Qn, preset, en, reset
  D_Flip_Flop d_ff_46 (.clk(and_14_out), .D(in_2));  // open: Q, Qn, preset, en, reset
  D_Flip_Flop d_ff_47 (.clk(and_15_out), .D(in_2));  // open: Q, Qn, preset, en, reset
  D_Flip_Flop d_ff_48 (.clk(and_16_out), .D(in_2));  // open: Q, Qn, preset, en, reset
  D_Flip_Flop d_ff_49 (.clk(and_1_out), .D(in_1));  // open: Q, Qn, preset, en, reset
  D_Flip_Flop d_ff_50 (.clk(and_2_out), .D(in_1));  // open: Q, Qn, preset, en, reset
  D_Flip_Flop d_ff_51 (.clk(and_3_out), .D(in_1));  // open: Q, Qn, preset, en, reset
  D_Flip_Flop d_ff_52 (.clk(and_4_out), .D(in_1));  // open: Q, Qn, preset, en, reset
  D_Flip_Flop d_ff_53 (.clk(and_5_out), .D(in_1));  // open: Q, Qn, preset, en, reset
  D_Flip_Flop d_ff_54 (.clk(and_6_out), .D(in_1));  // open: Q, Qn, preset, en, reset
  D_Flip_Flop d_ff_55 (.clk(and_7_out), .D(in_1));  // open: Q, Qn, preset, en, reset
  D_Flip_Flop d_ff_56 (.clk(and_8_out), .D(in_1));  // open: Q, Qn, preset, en, reset
  D_Flip_Flop d_ff_57 (.clk(and_9_out), .D(in_1));  // open: Q, Qn, preset, en, reset
  D_Flip_Flop d_ff_58 (.clk(and_10_out), .D(in_1));  // open: Q, Qn, preset, en, reset
  D_Flip_Flop d_ff_59 (.clk(and_11_out), .D(in_1));  // open: Q, Qn, preset, en, reset
  D_Flip_Flop d_ff_60 (.clk(and_12_out), .D(in_1));  // open: Q, Qn, preset, en, reset
  D_Flip_Flop d_ff_61 (.clk(and_13_out), .D(in_1));  // open: Q, Qn, preset, en, reset
  D_Flip_Flop d_ff_62 (.clk(and_14_out), .D(in_1));  // open: Q, Qn, preset, en, reset
  D_Flip_Flop d_ff_63 (.clk(and_15_out), .D(in_1));  // open: Q, Qn, preset, en, reset
  D_Flip_Flop d_ff_64 (.clk(and_16_out), .D(in_1));  // open: Q, Qn, preset, en, reset
endmodule

module flip_flop (
  input  in_1,
  output out_2
);

  wire undriven;

  D_Flip_Flop d_ff_1 (.clk(undriven), .D(in_1), .Q(out_2));  // open: Qn, preset, en, reset
endmodule
