// Logisim project nova_memoria.circ as structural Verilog: 1 circuit, main circuit main
module main (
);

  wire and_1_out, and_2_out, and_3_out, and_4_out, and_5_out, and_6_out, and_7_out, and_8_out, and_9_out,
       and_10_out, and_11_out, and_12_out, and_13_out, and_14_out, and_15_out, and_16_out, and_17_out,
       and_18_out, and_19_out, and_20_out, and_21_out, and_22_out, and_23_out, and_24_out, and_25_out,
       and_26_out, and_27_out, and_28_out, and_29_out, and_30_out, and_31_out, and_32_out, and_33_out,
       and_34_out, and_35_out, and_36_out, and_37_out, and_38_out, and_39_out, and_40_out, and_41_out,
       and_42_out, and_43_out, and_44_out, and_45_out, and_46_out, and_47_out, and_48_out, and_49_out,
       and_50_out, and_51_out, and_52_out, and_53_out, and_54_out, and_55_out, and_56_out, and_57_out,
       and_58_out, and_59_out, and_60_out, and_61_out, and_62_out, and_63_out, and_64_out, and_65_out,
       and_66_out, and_67_out, and_68_out, and_69_out, and_70_out, and_71_out, and_72_out, and_73_out,
       and_74_out, and_75_out, and_76_out, and_77_out, and_78_out, and_79_out, and_80_out, and_81_out,
       and_82_out, and_83_out, and_84_out, and_85_out, and_86_out, and_87_out, and_88_out, and_89_out,
       and_90_out, and_91_out, and_92_out, and_93_out, and_94_out, and_95_out, and_96_out, d_ff_1_q,
       d_ff_2_q, d_ff_3_q, d_ff_4_q, d_ff_5_q, d_ff_6_q, d_ff_7_q, d_ff_8_q, d_ff_9_q, d_ff_10_q, d_ff_11_q,
       d_ff_12_q, d_ff_13_q, d_ff_14_q, d_ff_15_q, d_ff_16_q, d_ff_17_q, d_ff_18_q, d_ff_19_q, d_ff_20_q,
       d_ff_21_q, d_ff_22_q, d_ff_23_q, d_ff_24_q, d_ff_25_q, d_ff_26_q, d_ff_27_q, d_ff_28_q, d_ff_29_q,
       d_ff_30_q, d_ff_31_q, d_ff_32_q, d_ff_33_q, d_ff_34_q, d_ff_35_q, d_ff_36_q, d_ff_37_q, d_ff_38_q,
       d_ff_39_q, d_ff_40_q, d_ff_41_q, d_ff_42_q, d_ff_43_q, d_ff_44_q, d_ff_45_q, d_ff_46_q, d_ff_47_q,
       d_ff_48_q, d_ff_49_q, d_ff_50_q, d_ff_51_q, d_ff_52_q, d_ff_53_q, d_ff_54_q, d_ff_55_q, d_ff_56_q,
       d_ff_57_q, d_ff_58_q, d_ff_59_q, d_ff_60_q, d_ff_61_q, d_ff_62_q, d_ff_63_q, d_ff_64_q, not_1_out,
       not_2_out, not_3_out, not_4_out, not_5_out, not_6_out, not_7_out, not_8_out, not_9_out, not_10_out,
       not_11_out, not_12_out, not_13_out, not_14_out, not_15_out, not_16_out, not_17_out, not_18_out,
       not_19_out, not_20_out, not_21_out, not_22_out, not_23_out, not_24_out, not_25_out, not_26_out,
       not_27_out, not_28_out, not_29_out, not_30_out, not_31_out, not_32_out, undriven, undriven_2,
       undriven_3, undriven_4, undriven_5, undriven_6, undriven_7, undriven_8;

  not not_1 (not_1_out, undriven);
  not not_2 (not_2_out, undriven_2);
  not not_3 (not_3_out, undriven_3);
  not not_4 (not_4_out, undriven_4);
  not not_5 (not_5_out, undriven);
  not not_6 (not_6_out, undriven_2);
  not not_7 (not_7_out, undriven_3);
  not not_8 (not_8_out, undriven);
  not not_9 (not_9_out, undriven_2);
  not not_10 (not_10_out, undriven_4);
  not not_11 (not_11_out, undriven);
  not not_12 (not_12_out, undriven_2);
  not not_13 (not_13_out, undriven);
  not not_14 (not_14_out, undriven_3);
  not not_15 (not_15_out, undriven_4);
  not not_16 (not_16_out, undriven);
  not not_17 (not_17_out, undriven_3);
  not not_18 (not_18_out, undriven);
  not not_19 (not_19_out, undriven_4);
  not not_20 (not_20_out, undriven);
  not not_21 (not_21_out, undriven_2);
  not not_22 (not_22_out, undriven_3);
  not not_23 (not_23_out, undriven_4);
  not not_24 (not_24_out, undriven_2);
  not not_25 (not_25_out, undriven_3);
  not not_26 (not_26_out, undriven_2);
  not not_27 (not_27_out, undriven_4);
  not not_28 (not_28_out, undriven_2);
  not not_29 (not_29_out, undriven_3);
  not not_30 (not_30_out, undriven_4);
  not not_31 (not_31_out, undriven_3);
  not not_32 (not_32_out, undriven_4);
  and and_1 (and_1_out, not_1_out, not_2_out, not_3_out, not_4_out);
  and and_2 (and_2_out, not_5_out, not_6_out, not_7_out, undriven_4);
  and and_3 (and_3_out, not_8_out, not_9_out, undriven_3, not_10_out);
  and and_4 (and_4_out, not_11_out, not_12_out, undriven_3, undriven_4);
  and and_5 (and_5_out, not_13_out, undriven_2, not_14_out, not_15_out);
  and and_6 (and_6_out, not_16_out, undriven_2, not_17_out, undriven_4);
  and and_7 (and_7_out, not_18_out, undriven_2, undriven_3, not_19_out);
  and and_8 (and_8_out, not_20_out, undriven_2, undriven_3, undriven_4);
  and and_9 (and_9_out, undriven, not_21_out, not_22_out, not_23_out);
  and and_10 (and_10_out, undriven, not_24_out, not_25_out, undriven_4);
  and and_11 (and_11_out, undriven, not_26_out, undriven_3, not_27_out);
  and and_12 (and_12_out, undriven, not_28_out, undriven_3, undriven_4);
  and and_13 (and_13_out, undriven, undriven_2, not_29_out, not_30_out);
  and and_14 (and_14_out, undriven, undriven_2, not_31_out, undriven_4);
  and and_15 (and_15_out, undriven, undriven_2, undriven_3, not_32_out);
  and and_16 (and_16_out, undriven, undriven_2, undriven_3, undriven_4);
  and and_17 (and_17_out, undriven_5, and_1_out);
  and and_18 (and_18_out, undriven_5, and_2_out);
  and and_19 (and_19_out, undriven_5, and_3_out);
  and and_20 (and_20_out, undriven_5, and_4_out);
  and and_21 (and_21_out, undriven_5, and_5_out);
  and and_22 (and_22_out, undriven_5, and_6_out);
  and and_23 (and_23_out, undriven_5, and_7_out);
  and and_24 (and_24_out, undriven_5, and_8_out);
  and and_25 (and_25_out, undriven_5, and_9_out);
  and and_26 (and_26_out, undriven_5, and_10_out);
  and and_27 (and_27_out, undriven_5, and_11_out);
  and and_28 (and_28_out, undriven_5, and_12_out);
  and and_29 (and_29_out, undriven_5, and_13_out);
  and and_30 (and_30_out, undriven_5, and_14_out);
  and and_31 (and_31_out, undriven_5, and_15_out);
  and and_32 (and_32_out, undriven_5, and_16_out);
  D_Flip_Flop d_ff_1 (.clk(and_17_out), .D(undriven_6), .Q(d_ff_1_q));  // open: Qn, preset, en, reset
  D_Flip_Flop d_ff_2 (.clk(and_18_out), .D(undriven_6), .Q(d_ff_2_q));  // open: Qn, preset, en, reset
  D_Flip_Flop d_ff_3 (.clk(and_19_out), .D(undriven_6), .Q(d_ff_3_q));  // open: Qn, preset, en, reset
  D_Flip_Flop d_ff_4 (.clk(and_20_out), .D(undriven_6), .Q(d_ff_4_q));  // open: Qn, preset, en, reset
  D_Flip_Flop d_ff_5 (.clk(and_21_out), .D(undriven_6), .Q(d_ff_5_q));  // open: Qn, preset, en, reset
  D_Flip_Flop d_ff_6 (.clk(and_22_out), .D(undriven_6), .Q(d_ff_6_q));  // open: Qn, preset, en, reset
  D_Flip_Flop d_ff_7 (.clk(and_23_out), .D(undriven_6), .Q(d_ff_7_q));  // open: Qn, preset, en, reset
  D_Flip_Flop d_ff_8 (.clk(and_24_out), .D(undriven_6), .Q(d_ff_8_q));  // open: Qn, preset, en, reset
  D_Flip_Flop d_ff_9 (.clk(and_25_out), .D(undriven_6), .Q(d_ff_9_q));  // open: Qn, preset, en, reset
  D_Flip_Flop d_ff_10 (.clk(and_26_out), .D(undriven_6), .Q(d_ff_10_q));  // open: Qn, preset, en, reset
  D_Flip_Flop d_ff_11 (.clk(and_27_out), .D(undriven_6), .Q(d_ff_11_q));  // open: Qn, preset, en, reset
  D_Flip_Flop d_ff_12 (.clk(and_28_out), .D(undriven_6), .Q(d_ff_12_q));  // open: Qn, preset, en, reset
  D_Flip_Flop d_ff_13 (.clk(and_29_out), .D(undriven_6), .Q(d_ff_13_q));  // open: Qn, preset, en, reset
  D_Flip_Flop d_ff_14 (.clk(and_30_out), .D(undriven_6), .Q(d_ff_14_q));  // open: Qn, preset, en, reset
  D_Flip_Flop d_ff_15 (.clk(and_31_out), .D(undriven_6), .Q(d_ff_15_q));  // open: Qn, preset, en, reset
  D_Flip_Flop d_ff_16 (.clk(and_32_out), .D(undriven_6), .Q(d_ff_16_q));  // open: Qn, preset, en, reset
  and and_33 (and_33_out, and_15_out, d_ff_15_q);
  and and_34 (and_34_out, and_16_out, d_ff_16_q);
  and and_35 (and_35_out, and_11_out, d_ff_11_q);
  and and_36 (and_36_out, and_12_out, d_ff_12_q);
  and and_37 (and_37_out, and_13_out, d_ff_13_q);
  and and_38 (and_38_out, and_14_out, d_ff_14_q);
  and and_39 (and_39_out, and_7_out, d_ff_7_q);
  and and_40 (and_40_out, and_8_out, d_ff_8_q);
  and and_41 (and_41_out, and_9_out, d_ff_9_q);
  and and_42 (and_42_out, and_10_out, d_ff_10_q);
  // OR_Gate or_1 has open pins: in0=and_34_out, in1=and_33_out, in2=and_38_out, in3=and_37_out, in4=and_36_out, in5=and_35_out, in6=and_42_out, in7=and_41_out, in8=and_40_out, in9=and_39_out, in10=and_46_out, in11=and_45_out, in12=and_44_out, in13=and_43_out, in14=and_48_out, in15=and_47_out, out=open
  and and_43 (and_43_out, and_3_out, d_ff_3_q);
  and and_44 (and_44_out, and_4_out, d_ff_4_q);
  and and_45 (and_45_out, and_5_out, d_ff_5_q);
  and and_46 (and_46_out, and_6_out, d_ff_6_q);
  and and_47 (and_47_out, and_1_out, d_ff_1_q);
  and and_48 (and_48_out, and_2_out, d_ff_2_q);
  D_Flip_Flop d_ff_17 (.clk(and_17_out), .D(undriven_7), .Q(d_ff_17_q));  // open: Qn, preset, en, reset
  D_Flip_Flop d_ff_18 (.clk(and_18_out), .D(undriven_7), .Q(d_ff_18_q));  // open: Qn, preset, en, reset
  D_Flip_Flop d_ff_19 (.clk(and_19_out), .D(undriven_7), .Q(d_ff_19_q));  // open: Qn, preset, en, reset
  D_Flip_Flop d_ff_20 (.clk(and_20_out), .D(undriven_7), .Q(d_ff_20_q));  // open: Qn, preset, en, reset
  D_Flip_Flop d_ff_21 (.clk(and_21_out), .D(undriven_7), .Q(d_ff_21_q));  // open: Qn, preset, en, reset
  D_Flip_Flop d_ff_22 (.clk(and_22_out), .D(undriven_7), .Q(d_ff_22_q));  // open: Qn, preset, en, reset
  D_Flip_Flop d_ff_23 (.clk(and_23_out), .D(undriven_7), .Q(d_ff_23_q));  // open: Qn, preset, en, reset
  D_Flip_Flop d_ff_24 (.clk(and_24_out), .D(undriven_7), .Q(d_ff_24_q));  // open: Qn, preset, en, reset
  D_Flip_Flop d_ff_25 (.clk(and_25_out), .D(undriven_7), .Q(d_ff_25_q));  // open: Qn, preset, en, reset
  D_Flip_Flop d_ff_26 (.clk(and_26_out), .D(undriven_7), .Q(d_ff_26_q));  // open: Qn, preset, en, reset
  D_Flip_Flop d_ff_27 (.clk(and_27_out), .D(undriven_7), .Q(d_ff_27_q));  // open: Qn, preset, en, reset
  D_Flip_Flop d_ff_28 (.clk(and_28_out), .D(undriven_7), .Q(d_ff_28_q));  // open: Qn, preset, en, reset
  D_Flip_Flop d_ff_29 (.clk(and_29_out), .D(undriven_7), .Q(d_ff_29_q));  // open: Qn, preset, en, reset
  D_Flip_Flop d_ff_30 (.clk(and_30_out), .D(undriven_7), .Q(d_ff_30_q));  // open: Qn, preset, en, reset
  D_Flip_Flop d_ff_31 (.clk(and_31_out), .D(undriven_7), .Q(d_ff_31_q));  // open: Qn, preset, en, reset
  D_Flip_Flop d_ff_32 (.clk(and_32_out), .D(undriven_7), .Q(d_ff_32_q));  // open: Qn, preset, en, reset
  and and_49 (and_49_out, and_14_out, d_ff_30_q);
  and and_50 (and_50_out, and_15_out, d_ff_31_q);
  and and_51 (and_51_out, and_16_out, d_ff_32_q);
  and and_52 (and_52_out, and_10_out, d_ff_26_q);
  and and_53 (and_53_out, and_11_out, d_ff_27_q);
  and and_54 (and_54_out, and_12_out, d_ff_28_q);
  and and_55 (and_55_out, and_13_out, d_ff_29_q);
  and and_56 (and_56_out, and_6_out, d_ff_22_q);
  and and_57 (and_57_out, and_7_out, d_ff_23_q);
  and and_58 (and_58_out, and_8_out, d_ff_24_q);
  and and_59 (and_59_out, and_9_out, d_ff_25_q);
  // OR_Gate or_2 has open pins: in0=and_51_out, in1=and_50_out, in2=and_49_out, in3=and_55_out, in4=and_54_out, in5=and_53_out, in6=and_52_out, in7=and_59_out, in8=and_58_out, in9=and_57_out, in10=and_56_out, in11=and_63_out, in12=and_62_out, in13=and_61_out, in14=and_60_out, in15=and_64_out, out=open
  and and_60 (and_60_out, and_2_out, d_ff_18_q);
  and and_61 (and_61_out, and_3_out, d_ff_19_q);
  and and_62 (and_62_out, and_4_out, d_ff_20_q);
  and and_63 (and_63_out, and_5_out, d_ff_21_q);
  and and_64 (and_64_out, and_1_out, d_ff_17_q);
  D_Flip_Flop d_ff_33 (.clk(and_17_out), .D(and_4_out), .Q(d_ff_33_q));  // open: Qn, preset, en, reset
  D_Flip_Flop d_ff_34 (.clk(and_18_out), .D(and_4_out), .Q(d_ff_34_q));  // open: Qn, preset, en, reset
  D_Flip_Flop d_ff_35 (.clk(and_19_out), .D(and_4_out), .Q(d_ff_35_q));  // open: Qn, preset, en, reset
  D_Flip_Flop d_ff_36 (.clk(and_20_out), .D(and_4_out), .Q(d_ff_36_q));  // open: Qn, preset, en, reset
  D_Flip_Flop d_ff_37 (.clk(and_21_out), .D(and_4_out), .Q(d_ff_37_q));  // open: Qn, preset, en, reset
  D_Flip_Flop d_ff_38 (.clk(and_22_out), .D(and_4_out), .Q(d_ff_38_q));  // open: Qn, preset, en, reset
  D_Flip_Flop d_ff_39 (.clk(and_23_out), .D(and_4_out), .Q(d_ff_39_q));  // open: Qn, preset, en, reset
  D_Flip_Flop d_ff_40 (.clk(and_24_out), .D(and_4_out), .Q(d_ff_40_q));  // open: Qn, preset, en, reset
  D_Flip_Flop d_ff_41 (.clk(and_25_out), .D(and_4_out), .Q(d_ff_41_q));  // open: Qn, preset, en, reset
  D_Flip_Flop d_ff_42 (.clk(and_26_out), .D(and_4_out), .Q(d_ff_42_q));  // open: Qn, preset, en, reset
  D_Flip_Flop d_ff_43 (.clk(and_27_out), .D(and_4_out), .Q(d_ff_43_q));  // open: Qn, preset, en, reset
  D_Flip_Flop d_ff_44 (.clk(and_28_out), .D(and_4_out), .Q(d_ff_44_q));  // open: Qn, preset, en, reset
  D_Flip_Flop d_ff_45 (.clk(and_29_out), .D(and_4_out), .Q(d_ff_45_q));  // open: Qn, preset, en, reset
  D_Flip_Flop d_ff_46 (.clk(and_30_out), .D(and_4_out), .Q(d_ff_46_q));  // open: Qn, preset, en, reset
  D_Flip_Flop d_ff_47 (.clk(and_31_out), .D(and_4_out), .Q(d_ff_47_q));  // open: Qn, preset, en, reset
  D_Flip_Flop d_ff_48 (.clk(and_32_out), .D(and_4_out), .Q(d_ff_48_q));  // open: Qn, preset, en, reset
  and and_65 (and_65_out, and_13_out, d_ff_45_q);
  and and_66 (and_66_out, and_14_out, d_ff_46_q);
  and and_67 (and_67_out, and_15_out, d_ff_47_q);
  and and_68 (and_68_out, and_16_out, d_ff_48_q);
  and and_69 (and_69_out, and_9_out, d_ff_41_q);
  and and_70 (and_70_out, and_10_out, d_ff_42_q);
  and and_71 (and_71_out, and_11_out, d_ff_43_q);
  and and_72 (and_72_out, and_12_out, d_ff_44_q);
  // OR_Gate or_3 has open pins: in0=and_68_out, in1=and_67_out, in2=and_66_out, in3=and_65_out, in4=and_72_out, in5=and_71_out, in6=and_70_out, in7=and_69_out, in8=and_76_out, in9=and_75_out, in10=and_74_out, in11=and_73_out, in12=and_80_out, in13=and_79_out, in14=and_78_out, in15=and_77_out, out=open
  and and_73 (and_73_out, and_5_out, d_ff_37_q);
  and and_74 (and_74_out, and_6_out, d_ff_38_q);
  and and_75 (and_75_out, and_7_out, d_ff_39_q);
  and and_76 (and_76_out, and_8_out, d_ff_40_q);
  and and_77 (and_77_out, and_1_out, d_ff_33_q);
  and and_78 (and_78_out, and_2_out, d_ff_34_q);
  and and_79 (and_79_out, and_3_out, d_ff_35_q);
  and and_80 (and_80_out, and_4_out, d_ff_36_q);
  D_Flip_Flop d_ff_49 (.clk(and_17_out), .D(undriven_8), .Q(d_ff_49_q));  // open: Qn, preset, en, reset
  D_Flip_Flop d_ff_50 (.clk(and_18_out), .D(undriven_8), .Q(d_ff_50_q));  // open: Qn, preset, en, reset
  D_Flip_Flop d_ff_51 (.clk(and_19_out), .D(undriven_8), .Q(d_ff_51_q));  // open: Qn, preset, en, reset
  D_Flip_Flop d_ff_52 (.clk(and_20_out), .D(undriven_8), .Q(d_ff_52_q));  // open: Qn, preset, en, reset
  D_Flip_Flop d_ff_53 (.clk(and_21_out), .D(undriven_8), .Q(d_ff_53_q));  // open: Qn, preset, en, reset
  D_Flip_Flop d_ff_54 (.clk(and_22_out), .D(undriven_8), .Q(d_ff_54_q));  // open: Qn, preset, en, reset
  D_Flip_Flop d_ff_55 (.clk(and_23_out), .D(undriven_8), .Q(d_ff_55_q));  // open: Qn, preset, en, reset
  D_Flip_Flop d_ff_56 (.clk(and_24_out), .D(undriven_8), .Q(d_ff_56_q));  // open: Qn, preset, en, reset
  D_Flip_Flop d_ff_57 (.clk(and_25_out), .D(undriven_8), .Q(d_ff_57_q));  // open: Qn, preset, en, reset
  D_Flip_Flop d_ff_58 (.clk(and_26_out), .D(undriven_8), .Q(d_ff_58_q));  // open: Qn, preset, en, reset
  D_Flip_Flop d_ff_59 (.clk(and_27_out), .D(undriven_8), .Q(d_ff_59_q));  // open: Qn, preset, en, reset
  D_Flip_Flop d_ff_60 (.clk(and_28_out), .D(undriven_8), .Q(d_ff_60_q));  // open: Qn, preset, en, reset
  D_Flip_Flop d_ff_61 (.clk(and_29_out), .D(undriven_8), .Q(d_ff_61_q));  // open: Qn, preset, en, reset
  D_Flip_Flop d_ff_62 (.clk(and_30_out), .D(undriven_8), .Q(d_ff_62_q));  // open: Qn, preset, en, reset
  D_Flip_Flop d_ff_63 (.clk(and_31_out), .D(undriven_8), .Q(d_ff_63_q));  // open: Qn, preset, en, reset
  D_Flip_Flop d_ff_64 (.clk(and_32_out), .D(undriven_8), .Q(d_ff_64_q));  // open: Qn, preset, en, reset
  and and_81 (and_81_out, and_16_out, d_ff_64_q);
  and and_82 (and_82_out, and_12_out, d_ff_60_q);
  and and_83 (and_83_out, and_13_out, d_ff_61_q);
  and and_84 (and_84_out, and_14_out, d_ff_62_q);
  and and_85 (and_85_out, and_15_out, d_ff_63_q);
  and and_86 (and_86_out, and_8_out, d_ff_56_q);
  and and_87 (and_87_out, and_9_out, d_ff_57_q);
  and and_88 (and_88_out, and_10_out, d_ff_58_q);
  and and_89 (and_89_out, and_11_out, d_ff_59_q);
  // OR_Gate or_4 has open pins: in0=and_81_out, in1=and_85_out, in2=and_84_out, in3=and_83_out, in4=and_82_out, in5=and_89_out, in6=and_88_out, in7=and_87_out, in8=and_86_out, in9=and_93_out, in10=and_92_out, in11=and_91_out, in12=and_90_out, in13=and_96_out, in14=and_95_out, in15=and_94_out, out=open
  and and_90 (and_90_out, and_4_out, d_ff_52_q);
  and and_91 (and_91_out, and_5_out, d_ff_53_q);
  and and_92 (and_92_out, and_6_out, d_ff_54_q);
  and and_93 (and_93_out, and_7_out, d_ff_55_q);
  and and_94 (and_94_out, and_1_out, d_ff_49_q);
  and and_95 (and_95_out, and_2_out, d_ff_50_q);
  and and_96 (and_96_out, and_3_out, d_ff_51_q);
endmodule
